// Digital circuit 4位寄存器.dig as structural Verilog
module \_4位寄存器  (
  input  [3:0] Din,
  input  WE,
  input  OE,
  input  Clock,
  output [3:0] DataStore,
  output [3:0] Dout
);

  Register #(.Bits(4)) register_1 (.D(Din), .C(Clock), .en(WE), .Q(DataStore));
  assign Dout = OE ? DataStore : 4'bz;  // Driver driver_1
endmodule
