// Digital circuit 8位ALU.dig as structural Verilog
module \_8位ALU  (
  input  [7:0] RegA,
  input  [7:0] RegB,
  input  OE,
  output [7:0] Dout,
  output Carry,
  output [7:0] ALUResult
);

  Add #(.Bits(8)) add_1 (.a(RegA), .b(RegB), .c_i(1'b0), .s(ALUResult), .c_o(Carry));
  assign Dout = OE ? ALUResult : 8'bz;  // Driver driver_1
endmodule
