// Digital circuit 8位加法器.dig as structural Verilog
module \_8位加法器  (
  input  [7:0] A,
  input  [7:0] B,
  output C,
  output [7:0] RESULT
);

  wire \全加器_子电路_1_carry , \全加器_子电路_2_p5 , \全加器_子电路_3_carry , \全加器_子电路_4_carry , \全加器_子电路_5_carry ,
       \全加器_子电路_6_carry , \半加器_子电路_1_carry ;

  \半加器_子电路  \u_半加器_子电路_1  (.In1(A[0]), .In2(B[0]), .Sum(RESULT[0]), .Carry(\半加器_子电路_1_carry ));
  \全加器_子电路  \u_全加器_子电路_1  (.C(\半加器_子电路_1_carry ), .B(A[1]), .A(B[1]), .SUM(RESULT[1]), .Carry(\全加器_子电路_1_carry ));
  // 全加器_子电路 全加器_子电路_2: pin names not known; wires that end beside it: \全加器_子电路_1_carry , A[2], B[2], RESULT[2], \全加器_子电路_2_p5 , A[3]
  \全加器_子电路  \u_全加器_子电路_3  (.C(\全加器_子电路_2_p5 ), .B(A[3]), .A(B[3]), .SUM(RESULT[3]), .Carry(\全加器_子电路_3_carry ));
  \全加器_子电路  \u_全加器_子电路_4  (.C(\全加器_子电路_3_carry ), .B(A[4]), .A(B[4]), .SUM(RESULT[4]), .Carry(\全加器_子电路_4_carry ));
  \全加器_子电路  \u_全加器_子电路_5  (.C(\全加器_子电路_4_carry ), .B(A[5]), .A(B[5]), .SUM(RESULT[5]), .Carry(\全加器_子电路_5_carry ));
  \全加器_子电路  \u_全加器_子电路_6  (.C(\全加器_子电路_5_carry ), .B(A[6]), .A(B[6]), .SUM(RESULT[6]), .Carry(\全加器_子电路_6_carry ));
  \全加器_子电路  \u_全加器_子电路_7  (.C(\全加器_子电路_6_carry ), .B(A[7]), .A(B[7]), .SUM(RESULT[7]), .Carry(C));
  PullDown #(.Bits(8)) pulldown_1 (.out(RESULT));
endmodule
