// Digital circuit 8位实用寄存器.dig as structural Verilog
module \_8位实用寄存器  (
  input  Clock,
  input  [7:0] Din,
  input  WE,
  input  OE,
  output [7:0] DOut,
  output [7:0] StoredData
);

  Register #(.Bits(8)) register_1 (.D(Din), .C(Clock), .en(WE), .Q(StoredData));
  assign DOut = OE ? StoredData : 8'bz;  // Driver driver_1
endmodule
