// Digital circuit 8位寄存器_子电路.dig as structural Verilog
module \_8位寄存器_子电路  (
  input  WE,
  input  [7:0] Din,
  output [7:0] Out
);

  \锁存器_子电路  _7 (.Din(Din[7]), .WE(WE), .Out(Out[7]));
  \锁存器_子电路  _6 (.Din(Din[6]), .WE(WE), .Out(Out[6]));
  \锁存器_子电路  _5 (.Din(Din[5]), .WE(WE), .Out(Out[5]));
  \锁存器_子电路  _4 (.Din(Din[4]), .WE(WE), .Out(Out[4]));
  \锁存器_子电路  _3 (.Din(Din[3]), .WE(WE), .Out(Out[3]));
  \锁存器_子电路  _2 (.Din(Din[2]), .WE(WE), .Out(Out[2]));
  \锁存器_子电路  _1 (.Din(Din[1]), .WE(WE), .Out(Out[1]));
  \锁存器_子电路  _0 (.Din(Din[0]), .WE(WE), .Out(Out[0]));
endmodule
