// Digital circuit CPU内部结构01.dig as structural Verilog
module \CPU内部结构01  (
  input  WE,
  input  OE,
  input  WE_2,
  input  OE_2,
  input  WE_3,
  input  OE_3,
  input  WE_4,
  input  OE_4,
  input  WE_5,
  input  OE_5,
  input  WE_6,
  input  OE_6,
  input  OE_7,
  output [7:0] RegB_Store,
  output [7:0] RegA_Store,
  output [7:0] RegC_Store,
  output [7:0] ALU_RESULT,
  output Carry,
  output [7:0] MBR,
  output [7:0] RegC_Out,
  output [7:0] IR,
  output [3:0] MAR,
  output [3:0] \CPU外部地址输出 ,
  output [7:0] \CPU外部数据输出 ,
  output [7:0] \CPU内部数据总线 
);

  wire Clock;
  wire [7:0] ALU_dout, \IR_CPU指令寄存器_dout , \寄存器A_dout , \寄存器B_dout ;

  Button u_Clock (.out(Clock));
  \_8位实用寄存器  \u_寄存器A  (.Clock(Clock), .Din(\CPU内部数据总线 ), .WE(WE), .OE(OE), .DOut(\寄存器A_dout ), .StoredData(RegA_Store));
  \_8位实用寄存器  \u_寄存器B  (
    .Clock(Clock), .Din(\CPU内部数据总线 ), .WE(WE_2), .OE(OE_2), .DOut(\寄存器B_dout ), .StoredData(RegB_Store));
  \_8位ALU  ALU (
    .RegA(\寄存器A_dout ), .RegB(\寄存器B_dout ), .OE(OE_7), .Dout(ALU_dout), .Carry(Carry), .ALUResult(ALU_RESULT));
  \_8位实用寄存器  \IR_CPU指令寄存器  (
    .Clock(Clock), .Din(\CPU内部数据总线 ), .WE(WE_5), .OE(OE_5), .DOut(\IR_CPU指令寄存器_dout ), .StoredData(IR));
  \_8位实用寄存器  \u_寄存器C  (
    .Clock(Clock), .Din(ALU_dout), .WE(WE_3), .OE(OE_3), .DOut(\CPU内部数据总线 ), .StoredData(RegC_Store));
  \_4位寄存器  \MAR_内存地址寄存器  (
    .Din(\IR_CPU指令寄存器_dout [7:4]), .WE(WE_6), .OE(OE_6), .Clock(Clock), .DataStore(\CPU外部地址输出 ), .Dout(MAR));
  \_8位实用寄存器  \u_内部缓存寄存器8位  (
    .Clock(Clock), .Din(\CPU内部数据总线 ), .WE(WE_4), .OE(OE_4), .DOut(\CPU内部数据总线 ), .StoredData(MBR));

  assign \CPU外部数据输出  = \CPU内部数据总线 ;
  assign RegC_Out = \CPU内部数据总线 ;

  // Notes on the sheet:
  //   8位CPU内部数据总线
  //   4位CPU外部地址总线
  //   8位CPU外部数据总线
endmodule
