// Digital circuit CPU内部结构03_修订版.dig as structural Verilog
module \CPU内部结构03_修订版  (
  input  WE,
  input  OE,
  input  WE_2,
  input  OE_2,
  input  WE_3,
  input  OE_3,
  input  WE_4,
  input  OE_4,
  input  WE_5,
  input  OE_5,
  input  WE_6,
  input  OE_6,
  input  OE_7,
  input  EN,
  input  OE_8,
  input  WE_7,
  input  OE_9,
  output [7:0] RegB_Store,
  output [7:0] RegA_Store,
  output [7:0] RegC_Store,
  output [7:0] ALU_RESULT,
  output Carry,
  output [7:0] MBR,
  output [7:0] RegC_Out,
  output [7:0] IR,
  output [3:0] MAR,
  output [7:0] \CPU外部数据输出 ,
  output [7:0] \CPU内部数据总线 ,
  output [1:0] \pc_2位存储 ,
  output [3:0] \pc_4位输出 ,
  output [3:0] \pc_4位存储 
);

  wire Clock;
  wire [3:0] \MAR_内存地址寄存器_datastore ;
  wire [7:0] ALU_dout, \寄存器A_dout , \寄存器B_dout ;
  wire [7:4] \IR_CPU指令寄存器_dout ;

  Button u_Clock (.out(Clock));
  \_8位实用寄存器  \u_寄存器A  (.Clock(Clock), .Din(\CPU内部数据总线 ), .WE(WE), .OE(OE), .DOut(\寄存器A_dout ), .StoredData(RegA_Store));
  \_8位实用寄存器  \u_寄存器B  (
    .Clock(Clock), .Din(\CPU内部数据总线 ), .WE(WE_2), .OE(OE_2), .DOut(\寄存器B_dout ), .StoredData(RegB_Store));
  \_8位ALU  ALU (
    .RegA(\寄存器A_dout ), .RegB(\寄存器B_dout ), .OE(OE_7), .Dout(ALU_dout), .Carry(Carry), .ALUResult(ALU_RESULT));
  \_8位实用寄存器  \IR_CPU指令寄存器  (
    .Clock(Clock), .Din(\CPU内部数据总线 ), .WE(WE_5), .OE(OE_5), .DOut({\IR_CPU指令寄存器_dout , \pc_4位输出 }),
    .StoredData(IR));
  Counter #(.Bits(2)) counter_1 (.en(EN), .C(Clock), .clr(1'b0), .out(\pc_2位存储 ));  // open: ovf
  \_8位实用寄存器  \u_寄存器C  (
    .Clock(Clock), .Din(ALU_dout), .WE(WE_3), .OE(OE_3), .DOut(\CPU内部数据总线 ), .StoredData(RegC_Store));
  assign \pc_4位输出  = OE_8 ? {2'b00, \pc_2位存储 } : 4'bz;  // Driver driver_1
  \_4位寄存器  \MAR_内存地址寄存器  (
    .Din(\pc_4位输出 ), .WE(WE_6), .OE(OE_6), .Clock(Clock), .DataStore(\MAR_内存地址寄存器_datastore ), .Dout(MAR));
  \_8位实用寄存器  \u_内部缓存寄存器8位  (
    .Clock(Clock), .Din(\CPU内部数据总线 ), .WE(WE_4), .OE(OE_4), .DOut(\CPU内部数据总线 ), .StoredData(MBR));
  EEPROMDualPort #(.AddrBits(4), .Bits(8)) eepromdualport_1 (
    .A(\MAR_内存地址寄存器_datastore ), .Din(\CPU内部数据总线 ), .str(WE_7), .C(Clock), .ld(OE_9), .D(\CPU内部数据总线 ));

  assign \CPU外部数据输出  = \CPU内部数据总线 ;
  assign \pc_4位存储  = {2'b00, \pc_2位存储 };
  assign RegC_Out = \CPU内部数据总线 ;

  // Notes on the sheet:
  //   Version3:
  //   加上内存(EEPROM)
  //   计数器
  //   代码执行哪一个地址的指令
  //   8位CPU内部数据总线
  //   4位CPU外部地址总线
  //   contents of eepromdualport_1 (hex, n*v repeats v):
  //   e,1f,20,3f,10*0,3,5
  //   8位CPU外部数据总线
endmodule
