// Digital circuit CPU内部结构04.dig as structural Verilog
module \CPU内部结构04  (
  input  clk,
  output [7:0] RegB_Store,
  output [7:0] RegA_Store,
  output [7:0] RegC_Store,
  output [7:0] ALU_RESULT,
  output Carry,
  output [7:0] MBR,
  output [7:0] RegC_Out,
  output [7:0] IR,
  output [3:0] MAR,
  output [7:0] \CPU外部数据输出 ,
  output [7:0] \CPU内部数据总线 ,
  output [1:0] \pc_2位存储 ,
  output [3:0] \pc_4位输出 ,
  output [3:0] \pc_4位存储 ,
  output [3:0] \opcode_操作码 ,
  output [2:0] \PC_3位存储 ,
  output [16:0] out_17
);

  wire [3:0] \MAR_内存地址寄存器_datastore ;
  wire [7:0] ALU_dout, \寄存器A_dout , \寄存器B_dout ;
  wire [7:4] \IR_CPU指令寄存器_dout ;

  Button Clock ();  // open: out
  Counter #(.Bits(3)) counter_1 (.en(1'b1), .C(clk), .clr(1'b0), .out(\PC_3位存储 ));  // open: ovf
  LookUpTable #(.Bits(17)) \CPU控制单元  (
    .in0(\PC_3位存储 [0]), .in1(\PC_3位存储 [1]), .in2(\PC_3位存储 [2]), .in3(IR[4]), .in4(IR[5]), .out(out_17));
  \_8位实用寄存器  \u_寄存器A  (
    .Clock(clk), .Din(\CPU内部数据总线 ), .WE(out_17[10]), .OE(out_17[11]), .DOut(\寄存器A_dout ),
    .StoredData(RegA_Store));
  \_8位实用寄存器  \u_寄存器B  (
    .Clock(clk), .Din(\CPU内部数据总线 ), .WE(out_17[12]), .OE(out_17[13]), .DOut(\寄存器B_dout ),
    .StoredData(RegB_Store));
  \_8位ALU  ALU (
    .RegA(\寄存器A_dout ), .RegB(\寄存器B_dout ), .OE(out_17[16]), .Dout(ALU_dout), .Carry(Carry),
    .ALUResult(ALU_RESULT));
  \_8位实用寄存器  \IR_CPU指令寄存器  (
    .Clock(clk), .Din(\CPU内部数据总线 ), .WE(out_17[8]), .OE(out_17[9]), .DOut({\IR_CPU指令寄存器_dout , \pc_4位输出 }),
    .StoredData(IR));
  Counter #(.Bits(2)) counter_2 (.en(out_17[1]), .C(clk), .clr(1'b0), .out(\pc_2位存储 ));  // open: ovf
  \_8位实用寄存器  \u_寄存器C  (
    .Clock(clk), .Din(ALU_dout), .WE(out_17[14]), .OE(out_17[15]), .DOut(\CPU内部数据总线 ), .StoredData(RegC_Store));
  assign \pc_4位输出  = out_17[0] ? {2'b00, \pc_2位存储 } : 4'bz;  // Driver driver_1
  \_4位寄存器  \MAR_内存地址寄存器  (
    .Din(\pc_4位输出 ), .WE(out_17[2]), .OE(out_17[3]), .Clock(clk), .DataStore(\MAR_内存地址寄存器_datastore ),
    .Dout(MAR));
  \_8位实用寄存器  \u_内部缓存寄存器8位  (
    .Clock(clk), .Din(\CPU内部数据总线 ), .WE(out_17[6]), .OE(out_17[7]), .DOut(\CPU内部数据总线 ), .StoredData(MBR));
  EEPROMDualPort #(.AddrBits(4), .Bits(8)) eepromdualport_1 (
    .A(\MAR_内存地址寄存器_datastore ), .Din(\CPU内部数据总线 ), .str(out_17[4]), .C(clk), .ld(out_17[5]), .D(\CPU内部数据总线 ));

  assign \CPU外部数据输出  = \CPU内部数据总线 ;
  assign \opcode_操作码  = IR[7:4];
  assign \pc_4位存储  = {2'b00, \pc_2位存储 };
  assign RegC_Out = \CPU内部数据总线 ;

  // Other names for the same wires on the sheet: Clock = clk; _0_CounterOE = out_17[0]; _1_CounterEN = out_17[1];
  //   _2_MARWE = out_17[2]; _3_MAROE = out_17[3]; _4_EEPROMWE = out_17[4]; _5_EEPROMOE = out_17[5];
  //   _6_MBRWE = out_17[6]; _7_MBROE = out_17[7]; _8_IRWE = out_17[8]; _9_IROE = out_17[9]; _10_RagAWE = out_17[10];
  //   _11_RegAOE = out_17[11]; _12_RagBWE = out_17[12]; _13_RegBOE = out_17[13]; _14_RagCWE = out_17[14];
  //   _15_RegCOE = out_17[15]; _16_ALUOE = out_17[16]

  // Notes on the sheet:
  //   clk: Hz: 10
  //   Version3:
  //   加上内存(EEPROM)
  //   Version3_改进:
  //   改进了计数器直接输出0
  //   Version4:
  //   加上控制单元
  //   contents of CPU控制单元 (hex, n*v repeats v):
  //   5,2,68,180,204,68,480,0,5,2,68,180,204,68,1080,0,5,2,68,180,16800
  //   ,0,0,0,5,2,68,180,8244,98
  //   控制单元
  //   基于查找表实现
  //   控制CPU内部自动存取指令
  //   计数器
  //   代码执行哪一个地址的指令
  //   0~3地址码
  //   4~7操作码
  //   8位CPU内部数据总线
  //   4位CPU外部地址总线
  //   contents of eepromdualport_1 (hex, n*v repeats v):
  //   e,1f,20,3f,10*0,3,5
  //   8位CPU外部数据总线
endmodule
