// Digital circuit EEPROM使用.dig as structural Verilog
module \EEPROM使用  (
  input  OE,
  input  WE,
  input  [7:0] Din,
  input  [15:0] Address,
  output [7:0] Dout
);

  wire Clock_out;

  Button Clock (.out(Clock_out));
  EEPROMDualPort #(.AddrBits(16), .Bits(8)) eepromdualport_1 (
    .A(Address), .Din(Din), .str(WE), .C(Clock_out), .ld(OE), .D(Dout));

  // Notes on the sheet:
  //   contents of eepromdualport_1 (hex, n*v repeats v):
  //   4,e,4
endmodule
