// Digital circuit test_8位ALU.dig as structural Verilog
module \test_8位ALU  (
  input  [7:0] RegB,
  input  [7:0] RegA,
  input  OE,
  output [7:0] Dout,
  output Carry,
  output [7:0] ALUResult
);

  \_8位ALU  \_8位alu_1  (.RegA(RegB), .RegB(RegA), .OE(OE), .Dout(Dout), .Carry(Carry), .ALUResult(ALUResult));
endmodule
