// Digital circuit 与或非门.dig as structural Verilog
module \与或非门  (
  input  in_1,
  input  in_2,
  input  in_4,
  input  in_5,
  input  in_7,
  input  in_8,
  input  in_10,
  input  in_11,
  input  in_13,
  input  in_15,
  output out_3,
  output out_6,
  output out_9,
  output out_12,
  output out_14,
  output out_16
);

  wire relaydt_1_p5;

  // RelayDT relaydt_1: pin names not known; wires that end beside it: in_10, 1'b1, in_11, 1'b0, relaydt_1_p5, 1'b0
  // RelayDT relaydt_2: pin names not known; wires that end beside it: relaydt_1_p5, out_12
  and and_1 (out_3, in_1, in_2);
  or or_1 (out_6, in_4, in_5);
  not not_1 (out_16, in_15);
  // RelayDT relaydt_3: pin names not known; wires that end beside it: in_7, in_8, 1'b0, out_9, 1'b0
  // RelayDT relaydt_4: pin names not known; wires that end beside it: 1'b1, out_9
  // RelayDT relaydt_5: pin names not known; wires that end beside it: in_13, 1'b1, 1'b0, out_14
endmodule
