// Digital circuit 与门.dig as structural Verilog
module \与门  (
  input  A,
  input  B,
  output out_3
);

  wire relaydt_1_p4;

  // RelayDT relaydt_1: pin names not known; wires that end beside it: A, 1'b1, 1'b0, relaydt_1_p4
  // RelayDT relaydt_2: pin names not known; wires that end beside it: B, relaydt_1_p4, 1'b0, out_3
endmodule
