// Digital circuit 全加器_子电路.dig as structural Verilog
module \全加器_子电路  (
  input  C,
  input  B,
  input  A,
  output SUM,
  output Carry
);

  wire \半加器_子电路_1_carry , \半加器_子电路_1_sum , \半加器_子电路_2_carry ;

  \半加器_子电路  \u_半加器_子电路_1  (.In1(B), .In2(A), .Sum(\半加器_子电路_1_sum ), .Carry(\半加器_子电路_1_carry ));
  \半加器_子电路  \u_半加器_子电路_2  (.In1(C), .In2(\半加器_子电路_1_sum ), .Sum(SUM), .Carry(\半加器_子电路_2_carry ));
  or or_1 (Carry, \半加器_子电路_2_carry , \半加器_子电路_1_carry );
endmodule
