// Digital circuit 内存单元_子电路.dig as structural Verilog
module \内存单元_子电路  (
  input  str,
  input  Din,
  input  ld,
  input  column,
  input  row,
  output Out
);

  wire and_1_out, and_2_out, and_3_out, \锁存器_子电路_1_out ;

  and and_1 (and_1_out, str, and_3_out);
  and and_2 (and_2_out, ld, and_3_out);
  \锁存器_子电路  \u_锁存器_子电路_1  (.Din(Din), .WE(and_1_out), .Out(\锁存器_子电路_1_out ));
  and and_3 (and_3_out, column, row);
  assign Out = and_2_out ? \锁存器_子电路_1_out  : 1'bz;  // Driver driver_1
endmodule
