// Digital circuit 内存条.dig as structural Verilog
module \内存条  (
  input  Din,
  input  OE,
  input  str,
  input  row1,
  input  row2,
  input  row3,
  input  row0,
  input  column1,
  input  column2,
  input  column3,
  input  column0,
  output Dout
);

  \内存单元_子电路  \u_内存单元_子电路_1  (.str(str), .Din(Din), .ld(OE), .column(column0), .row(row0), .Out(Dout));
  \内存单元_子电路  \u_内存单元_子电路_2  (.str(str), .Din(Din), .ld(OE), .column(column0), .row(row1), .Out(Dout));
  // 内存单元_子电路 内存单元_子电路_3: pin names not known; wires that end beside it: str, Din, OE, column0, row2, Dout
  \内存单元_子电路  \u_内存单元_子电路_4  (.str(str), .Din(Din), .ld(OE), .column(column0), .row(row3), .Out(Dout));
  \内存单元_子电路  \u_内存单元_子电路_5  (.str(str), .Din(Din), .ld(OE), .column(column1), .row(row0), .Out(Dout));
  \内存单元_子电路  \u_内存单元_子电路_6  (.str(str), .Din(Din), .ld(OE), .column(column1), .row(row1), .Out(Dout));
  \内存单元_子电路  \u_内存单元_子电路_7  (.str(str), .Din(Din), .ld(OE), .column(column1), .row(row2), .Out(Dout));
  \内存单元_子电路  \u_内存单元_子电路_8  (.str(str), .Din(Din), .ld(OE), .column(column1), .row(row3), .Out(Dout));
  \内存单元_子电路  \u_内存单元_子电路_9  (.str(str), .Din(Din), .ld(OE), .column(column2), .row(row0), .Out(Dout));
  \内存单元_子电路  \u_内存单元_子电路_10  (.str(str), .Din(Din), .ld(OE), .column(column2), .row(row1), .Out(Dout));
  \内存单元_子电路  \u_内存单元_子电路_11  (.str(str), .Din(Din), .ld(OE), .column(column2), .row(row2), .Out(Dout));
  \内存单元_子电路  \u_内存单元_子电路_12  (.str(str), .Din(Din), .ld(OE), .column(column2), .row(row3), .Out(Dout));
  \内存单元_子电路  \u_内存单元_子电路_13  (.str(str), .Din(Din), .ld(OE), .column(column3), .row(row0), .Out(Dout));
  \内存单元_子电路  \u_内存单元_子电路_14  (.str(str), .Din(Din), .ld(OE), .column(column3), .row(row1), .Out(Dout));
  \内存单元_子电路  \u_内存单元_子电路_15  (.str(str), .Din(Din), .ld(OE), .column(column3), .row(row2), .Out(Dout));
  \内存单元_子电路  \u_内存单元_子电路_16  (.str(str), .Din(Din), .ld(OE), .column(column3), .row(row3), .Out(Dout));
endmodule
