// Digital circuit 半加器_子电路.dig as structural Verilog
module \半加器_子电路  (
  input  In1,
  input  In2,
  output Sum,
  output Carry
);

  xor xor_1 (Sum, In1, In2);
  and and_1 (Carry, In1, In2);
endmodule
