// Digital circuit 寄存器总线.dig as structural Verilog
module \寄存器总线  (
  input  WE,
  input  [7:0] Din,
  input  OE,
  output [7:0] Out
);

  wire \锁存器_子电路_1_out , \锁存器_子电路_2_out , \锁存器_子电路_3_out , \锁存器_子电路_4_out , \锁存器_子电路_5_out , \锁存器_子电路_6_out ,
       \锁存器_子电路_7_out , \锁存器_子电路_8_out ;

  assign Out[7] = OE ? \锁存器_子电路_1_out  : 1'bz;  // Driver driver_1
  \锁存器_子电路  \u_锁存器_子电路_1  (.Din(Din[7]), .WE(WE), .Out(\锁存器_子电路_1_out ));
  \锁存器_子电路  \u_锁存器_子电路_2  (.Din(Din[6]), .WE(WE), .Out(\锁存器_子电路_2_out ));
  assign Out[6] = OE ? \锁存器_子电路_2_out  : 1'bz;  // Driver driver_2
  assign Out[5] = OE ? \锁存器_子电路_3_out  : 1'bz;  // Driver driver_3
  \锁存器_子电路  \u_锁存器_子电路_3  (.Din(Din[5]), .WE(WE), .Out(\锁存器_子电路_3_out ));
  assign Out[4] = OE ? \锁存器_子电路_4_out  : 1'bz;  // Driver driver_4
  \锁存器_子电路  \u_锁存器_子电路_4  (.Din(Din[4]), .WE(WE), .Out(\锁存器_子电路_4_out ));
  assign Out[3] = OE ? \锁存器_子电路_5_out  : 1'bz;  // Driver driver_5
  \锁存器_子电路  \u_锁存器_子电路_5  (.Din(Din[3]), .WE(WE), .Out(\锁存器_子电路_5_out ));
  \锁存器_子电路  \u_锁存器_子电路_6  (.Din(Din[2]), .WE(WE), .Out(\锁存器_子电路_6_out ));
  assign Out[2] = OE ? \锁存器_子电路_6_out  : 1'bz;  // Driver driver_6
  assign Out[1] = OE ? \锁存器_子电路_7_out  : 1'bz;  // Driver driver_7
  \锁存器_子电路  \u_锁存器_子电路_7  (.Din(Din[1]), .WE(WE), .Out(\锁存器_子电路_7_out ));
  assign Out[0] = OE ? \锁存器_子电路_8_out  : 1'bz;  // Driver driver_8
  \锁存器_子电路  \u_锁存器_子电路_8  (.Din(Din[0]), .WE(WE), .Out(\锁存器_子电路_8_out ));
  PullDown #(.Bits(8)) pulldown_1 (.out(Out));
endmodule
