// Digital circuit 带时钟的锁存器.dig as structural Verilog
module \带时钟的锁存器  (
  input  Din,
  input  Din_2,
  output Out,
  output Out_2
);

  wire Clock_2_out, Clock_out, not_1_out, not_2_out, \锁存器_子电路_1_out , \锁存器_子电路_2_out ;

  Button Clock (.out(Clock_out));
  Button Clock_2 (.out(Clock_2_out));
  \锁存器_子电路  \u_锁存器_子电路_1  (.Din(Din_2), .WE(not_1_out), .Out(\锁存器_子电路_1_out ));
  not not_1 (not_1_out, Clock_out);
  \锁存器_子电路  \u_锁存器_子电路_2  (.Din(Din), .WE(Clock_2_out), .Out(\锁存器_子电路_2_out ));
  not not_2 (not_2_out, Clock_2_out);
  \锁存器_子电路  \u_锁存器_子电路_3  (.Din(\锁存器_子电路_1_out ), .WE(Clock_out), .Out(Out_2));
  \锁存器_子电路  \u_锁存器_子电路_4  (.Din(\锁存器_子电路_2_out ), .WE(not_2_out), .Out(Out));
endmodule
