// Digital circuit 异或门.dig as structural Verilog
module \异或门  (
  input  in_1,
  input  in_2,
  input  in_4,
  input  in_5,
  output out_3,
  output out_6
);

  wire relaydt_1_p3, relaydt_1_p4;

  xor xor_1 (out_6, in_4, in_5);
  // RelayDT relaydt_1: pin names not known; wires that end beside it: in_1, 1'b1, relaydt_1_p3, relaydt_1_p4
  // RelayDT relaydt_2: pin names not known; wires that end beside it: 1'b0, in_2, relaydt_1_p4, relaydt_1_p3, 1'b0, out_3
endmodule
