// Digital circuit 时钟边沿触发锁存器_子电路.dig as structural Verilog
module \时钟边沿触发锁存器_子电路  (
  input  Din,
  output Out
);

  wire Clock_out, not_1_out, \锁存器_子电路_1_out ;

  Button Clock (.out(Clock_out));
  \锁存器_子电路  \u_锁存器_子电路_1  (.Din(Din), .WE(Clock_out), .Out(\锁存器_子电路_1_out ));
  not not_1 (not_1_out, Clock_out);
  \锁存器_子电路  \u_锁存器_子电路_2  (.Din(\锁存器_子电路_1_out ), .WE(not_1_out), .Out(Out));
endmodule
