// Digital circuit 记忆电路.dig as structural Verilog
module \记忆电路  (
  output out_1
);

  wire Reset_p2;

  // SwitchDT Set: pin names not known; wires that end beside it: 1'b1, out_1
  // SwitchDT Reset: pin names not known; wires that end beside it: out_1, Reset_p2, Reset_p2, 1'b0
  // RelayDT relaydt_1: pin names not known; wires that end beside it: 1'b1, out_1
endmodule
