// Digital circuit 锁存器.dig as structural Verilog
module \锁存器  (
  input  Din,
  input  WE,
  input  Din_2,
  input  WE_2,
  output Out,
  output Out_2
);

  wire and_1_out, and_2_out, not_1_out, not_2_out, or_1_out;

  \锁存器_子电路  \u_锁存器_子电路_1  (.Din(Din_2), .WE(WE_2), .Out(Out_2));
  not not_1 (not_1_out, Din);
  and and_1 (and_1_out, Din, WE);
  and and_2 (and_2_out, not_1_out, WE);
  or or_1 (or_1_out, Out, and_1_out);
  not not_2 (not_2_out, and_2_out);
  and and_3 (Out, or_1_out, not_2_out);
endmodule
